// Logisim project Flip Flop JK.circ as structural Verilog: 1 circuit, main circuit main
module main (
  input  PRESET,
  input  J,
  input  CLOCK,
  input  K,
  input  CLEAR,
  output Q,
  output Q_2
);

  wire nand_1_out, nand_2_out, not_1_out, not_2_out, not_3_out, not_4_out, Q1_2_out, Q1_out, r_out, S_out;

  not not_1 (not_1_out, CLOCK);
  not not_2 (not_2_out, PRESET);
  nand nand_1 (nand_1_out, Q_2, J, not_1_out);
  nand nand_2 (nand_2_out, not_1_out, K, Q);
  not not_3 (not_3_out, CLEAR);
  nand Q1 (Q1_out, not_2_out, nand_1_out, Q1_2_out);
  nand Q1_2 (Q1_2_out, Q1_out, nand_2_out, not_3_out);
  not not_4 (not_4_out, not_1_out);
  nand S (S_out, Q1_out, not_4_out, not_3_out);
  nand r (r_out, not_2_out, not_4_out, Q1_2_out);
  nand nand_3 (Q, not_2_out, S_out, Q_2);
  nand nand_4 (Q_2, Q, r_out, not_3_out);
endmodule
