// Logisim project Multiplexador_4x1.circ as structural Verilog: 1 circuit, main circuit main
module main (
  input  ENTRADA_1,
  input  ENTRADA_2,
  input  ENTRADA_3,
  input  SELETOR_1,
  input  ENTRADA_4,
  input  SELETOR_2,
  output SAIDA
);

  wire and_1_out, and_2_out, and_3_out, and_4_out, not_1_out, not_2_out;

  not not_1 (not_1_out, SELETOR_2);
  not not_2 (not_2_out, SELETOR_1);
  and and_1 (and_1_out, ENTRADA_1, not_1_out, not_2_out);
  and and_2 (and_2_out, ENTRADA_2, not_1_out, SELETOR_1);
  and and_3 (and_3_out, ENTRADA_3, not_2_out, SELETOR_2);
  and and_4 (and_4_out, ENTRADA_4, SELETOR_1, SELETOR_2);
  or or_1 (SAIDA, and_1_out, and_2_out, and_3_out, and_4_out);
endmodule
