// Logisim project XOR.circ as structural Verilog: 1 circuit, main circuit main
module main (
  input  Entrada_A,
  input  ENTRADA_B,
  output SAIDA
);

  wire and_1_out, and_2_out, not_1_out, not_2_out;

  not not_1 (not_1_out, Entrada_A);
  not not_2 (not_2_out, ENTRADA_B);
  and and_1 (and_1_out, not_1_out, ENTRADA_B);
  and and_2 (and_2_out, Entrada_A, not_2_out);
  or or_1 (SAIDA, and_1_out, and_2_out);
endmodule
