// Logisim project somador_8_bits_4.circ as structural Verilog: 1 circuit, main circuit main
module main (
  input  [7:0] A,
  output [8:0] Saida
);

  wire full_adder_1_carry_out, full_adder_2_carry_out, full_adder_3_carry_out, full_adder_4_carry_out,
       full_adder_5_carry_out, full_adder_6_carry_out, full_adder_7_carry_out;

  full_adder full_adder_1 (.Carry_Out(full_adder_1_carry_out), .S(Saida[0]), .A(A[0]), .B(1'b0), .Carry_In(1'b0));
  full_adder full_adder_2 (
    .Carry_Out(full_adder_2_carry_out), .S(Saida[1]), .A(A[1]), .B(1'b0), .Carry_In(full_adder_1_carry_out));
  full_adder full_adder_3 (
    .Carry_Out(full_adder_3_carry_out), .S(Saida[2]), .A(A[2]), .B(1'b1), .Carry_In(full_adder_2_carry_out));
  full_adder full_adder_4 (
    .Carry_Out(full_adder_4_carry_out), .S(Saida[3]), .A(A[3]), .B(1'b0), .Carry_In(full_adder_3_carry_out));
  full_adder full_adder_5 (
    .Carry_Out(full_adder_5_carry_out), .S(Saida[4]), .A(A[4]), .B(1'b0), .Carry_In(full_adder_4_carry_out));
  full_adder full_adder_6 (
    .Carry_Out(full_adder_6_carry_out), .S(Saida[5]), .A(A[5]), .B(1'b0), .Carry_In(full_adder_5_carry_out));
  full_adder full_adder_7 (
    .Carry_Out(full_adder_7_carry_out), .S(Saida[6]), .A(A[6]), .B(1'b0), .Carry_In(full_adder_6_carry_out));
  full_adder full_adder_8 (.Carry_Out(Saida[8]), .S(Saida[7]), .A(A[7]), .B(1'b0), .Carry_In(full_adder_7_carry_out));
endmodule
