// Logisim project Memoria_RAM.circ as structural Verilog: 9 circuits, main circuit MEMORIA_RAM_8X8
module MEMORIA_RAM_8X8 (
  input  [7:0] Entrada,
  input  Clear,
  input  [2:0] Selector,
  input  Enable,
  output [7:0] Saida
);

  wire Clock_out, demux_8x1_1_s, demux_8x1_1_s_2, demux_8x1_1_s_3, demux_8x1_1_s_4, demux_8x1_1_s_5,
       demux_8x1_1_s_6, demux_8x1_1_s_7, demux_8x1_1_s_8, not_1_out;
  wire [7:0] _1_q, _2_q, _3_q, _4_q, _5_q, _6_q, _7_q, _8_q;

  Clock Clock (.out(Clock_out));
  not not_1 (not_1_out, Enable);
  DEMUX_8X1 demux_8x1_1 (
    .D(Clock_out), .Select(Selector), .S(demux_8x1_1_s), .Load(not_1_out), .S_2(demux_8x1_1_s_2),
    .S_3(demux_8x1_1_s_3), .S_4(demux_8x1_1_s_4), .S_5(demux_8x1_1_s_5), .S_6(demux_8x1_1_s_6),
    .S_7(demux_8x1_1_s_7), .S_8(demux_8x1_1_s_8));
  REGISTRADOR_8BITS _1 (.Data(Entrada), .Clock(demux_8x1_1_s), .Clear(Clear), .Q(_1_q));
  REGISTRADOR_8BITS _2 (.Data(Entrada), .Clock(demux_8x1_1_s_2), .Clear(Clear), .Q(_2_q));
  REGISTRADOR_8BITS _3 (.Data(Entrada), .Clock(demux_8x1_1_s_3), .Clear(Clear), .Q(_3_q));
  REGISTRADOR_8BITS _4 (.Data(Entrada), .Clock(demux_8x1_1_s_4), .Clear(Clear), .Q(_4_q));
  REGISTRADOR_8BITS _5 (.Data(Entrada), .Clock(demux_8x1_1_s_5), .Clear(Clear), .Q(_5_q));
  MUX_8X1_8BITS mux_8x1_8bits_1 (
    .A0(_1_q), .A1(_2_q), .A2(_3_q), .A3(_4_q), .A4(_5_q), .A5(_6_q), .A6(_7_q), .A7(_8_q),
    .Seletor(Selector), .Saida(Saida), .Load(Enable));
  REGISTRADOR_8BITS _6 (.Data(Entrada), .Clock(demux_8x1_1_s_6), .Clear(Clear), .Q(_6_q));
  REGISTRADOR_8BITS _7 (.Data(Entrada), .Clock(demux_8x1_1_s_7), .Clear(Clear), .Q(_7_q));
  REGISTRADOR_8BITS _8 (.Data(Entrada), .Clock(demux_8x1_1_s_8), .Clear(Clear), .Q(_8_q));

  // Notes on the sheet:
  //   ENABLE = 0: Escrita
  //   ENABLE = 1: Leitura
  //   000 = A0
  //   001 = A1
  //   010 = A2
  //   011 = A3
  //   100 = A4
  //   101 = A5
  //   110 = A6
  //   111 = A7
endmodule

module FF_JK (
  input  Preset,
  input  J,
  input  Clock,
  input  K,
  input  Clear,
  output Q,
  output nQ
);

  wire nand_1_out, nand_2_out, nand_3_out, nand_4_out, nand_5_out, nand_6_out, not_1_out, not_2_out,
       not_3_out;

  nand nand_1 (nand_1_out, J, nQ, Clock);
  not not_1 (not_1_out, Clock);
  nand nand_2 (nand_2_out, Clock, Q, K);
  not not_2 (not_2_out, Preset);
  not not_3 (not_3_out, Clear);
  nand nand_3 (nand_3_out, not_2_out, nand_1_out, nand_4_out);
  nand nand_4 (nand_4_out, nand_3_out, nand_2_out, not_3_out);
  nand nand_5 (nand_5_out, not_3_out, nand_3_out, not_1_out);
  nand nand_6 (nand_6_out, not_1_out, nand_4_out, not_2_out);
  nand nand_7 (Q, not_2_out, nand_5_out, nQ);
  nand nand_8 (nQ, Q, nand_6_out, not_3_out);
endmodule

module FF_D (
  input  D,
  input  CLK,
  input  _1,
  input  _0,
  output out_5,
  output out_6
);

  wire not_1_out;

  not not_1 (not_1_out, D);
  FF_JK ff_jk_1 (.Preset(_1), .J(D), .Clock(CLK), .K(not_1_out), .Clear(_0), .Q(out_5), .nQ(out_6));
endmodule

module REGISTRADOR_8BITS (
  input  [7:0] Data,
  input  Clock,
  input  Clear,
  output [7:0] Q
);

  FF_D ff_d_1 (.D(Data[0]), .CLK(Clock), .out_5(Q[0]), ._1(1'b0), ._0(Clear));  // open: out_6
  FF_D ff_d_2 (.D(Data[1]), .CLK(Clock), .out_5(Q[1]), ._1(1'b0), ._0(Clear));  // open: out_6
  FF_D ff_d_3 (.D(Data[2]), .CLK(Clock), .out_5(Q[2]), ._1(1'b0), ._0(Clear));  // open: out_6
  FF_D ff_d_4 (.D(Data[3]), .CLK(Clock), .out_5(Q[3]), ._1(1'b0), ._0(Clear));  // open: out_6
  FF_D ff_d_5 (.D(Data[4]), .CLK(Clock), .out_5(Q[4]), ._1(1'b0), ._0(Clear));  // open: out_6
  FF_D ff_d_6 (.D(Data[5]), .CLK(Clock), .out_5(Q[5]), ._1(1'b0), ._0(Clear));  // open: out_6
  FF_D ff_d_7 (.D(Data[6]), .CLK(Clock), .out_5(Q[6]), ._1(1'b0), ._0(Clear));  // open: out_6
  FF_D ff_d_8 (.D(Data[7]), .CLK(Clock), .out_5(Q[7]), ._1(1'b0), ._0(Clear));  // open: out_6
endmodule

module DEMUX_8X1 (
  input  D,
  input  Load,
  input  [2:0] Select,
  output S,
  output S_2,
  output S_3,
  output S_4,
  output S_5,
  output S_6,
  output S_7,
  output S_8
);

  wire and_1_out, not_1_out, not_2_out, not_3_out, not_4_out, not_5_out, not_6_out, not_7_out, not_8_out,
       not_9_out, not_10_out, not_11_out, not_12_out;

  and and_1 (and_1_out, D, Load);
  not not_1 (not_1_out, Select[0]);
  not not_2 (not_2_out, Select[1]);
  not not_3 (not_3_out, Select[2]);
  not not_4 (not_4_out, Select[1]);
  not not_5 (not_5_out, Select[2]);
  not not_6 (not_6_out, Select[0]);
  not not_7 (not_7_out, Select[2]);
  not not_8 (not_8_out, Select[2]);
  not not_9 (not_9_out, Select[0]);
  not not_10 (not_10_out, Select[1]);
  not not_11 (not_11_out, Select[1]);
  not not_12 (not_12_out, Select[0]);
  and _0 (S, not_1_out, not_2_out, not_3_out, and_1_out);
  and _1 (S_2, Select[0], not_4_out, not_5_out, and_1_out);
  and _2 (S_3, not_6_out, Select[1], not_7_out, and_1_out);
  and _3 (S_4, Select[0], Select[1], not_8_out, and_1_out);
  and _4 (S_5, not_9_out, not_10_out, Select[2], and_1_out);
  and _5 (S_6, Select[0], not_11_out, Select[2], and_1_out);
  and _6 (S_7, not_12_out, Select[1], Select[2], and_1_out);
  and _7 (S_8, Select[0], Select[1], Select[2], and_1_out);
endmodule

module MUX_2X1 (
  input  I0,
  input  I1,
  input  Load,
  input  Select,
  output out_5
);

  wire and_1_out, and_2_out, not_1_out, or_1_out;

  not not_1 (not_1_out, Select);
  and and_1 (and_1_out, not_1_out, I0);
  and and_2 (and_2_out, I1, Select);
  or or_1 (or_1_out, and_1_out, and_2_out);
  and and_3 (out_5, or_1_out, Load);
endmodule

module MUX_2X1_8BITS (
  input  [7:0] in_1,
  input  [7:0] in_2,
  input  Select,
  input  Load,
  output [7:0] out_5
);

  MUX_2X1 mux_2x1_1 (.I0(in_1[0]), .I1(in_2[0]), .Select(Select), .out_5(out_5[0]), .Load(Load));
  MUX_2X1 mux_2x1_2 (.I0(in_1[1]), .I1(in_2[1]), .Select(Select), .out_5(out_5[1]), .Load(Load));
  MUX_2X1 mux_2x1_3 (.I0(in_1[2]), .I1(in_2[2]), .Select(Select), .out_5(out_5[2]), .Load(Load));
  MUX_2X1 mux_2x1_4 (.I0(in_1[3]), .I1(in_2[3]), .Select(Select), .out_5(out_5[3]), .Load(Load));
  MUX_2X1 mux_2x1_5 (.I0(in_1[4]), .I1(in_2[4]), .Select(Select), .out_5(out_5[4]), .Load(Load));
  MUX_2X1 mux_2x1_6 (.I0(in_1[5]), .I1(in_2[5]), .Select(Select), .out_5(out_5[5]), .Load(Load));
  MUX_2X1 mux_2x1_7 (.I0(in_1[6]), .I1(in_2[6]), .Select(Select), .out_5(out_5[6]), .Load(Load));
  MUX_2X1 mux_2x1_8 (.I0(in_1[7]), .I1(in_2[7]), .Select(Select), .out_5(out_5[7]), .Load(Load));
endmodule

module MUX_4X1_8BITS (
  input  [7:0] A0,
  input  [7:0] A1,
  input  [7:0] A2,
  input  [7:0] A3,
  input  [1:0] Select,
  input  Load,
  output [7:0] Saida
);

  wire [7:0] mux_2x1_8bits_1_out_5, mux_2x1_8bits_2_out_5;

  MUX_2X1_8BITS mux_2x1_8bits_1 (.in_1(A0), .in_2(A1), .Select(Select[0]), .out_5(mux_2x1_8bits_1_out_5), .Load(Load));
  MUX_2X1_8BITS mux_2x1_8bits_2 (.in_1(A2), .in_2(A3), .Select(Select[0]), .out_5(mux_2x1_8bits_2_out_5), .Load(Load));
  MUX_2X1_8BITS mux_2x1_8bits_3 (
    .in_1(mux_2x1_8bits_1_out_5), .in_2(mux_2x1_8bits_2_out_5), .Select(Select[1]), .out_5(Saida), .Load(Load));
endmodule

module MUX_8X1_8BITS (
  input  [7:0] A0,
  input  [7:0] A1,
  input  [7:0] A2,
  input  [7:0] A3,
  input  [7:0] A4,
  input  [7:0] A5,
  input  [7:0] A6,
  input  [7:0] A7,
  input  [2:0] Seletor,
  input  Load,
  output [7:0] Saida
);

  wire [7:0] mux_4x1_8bits_1_saida, mux_4x1_8bits_2_saida;

  MUX_4X1_8BITS mux_4x1_8bits_1 (
    .A0(A0), .A1(A1), .A2(A2), .A3(A3), .Select(Seletor[1:0]), .Saida(mux_4x1_8bits_1_saida), .Load(Load));
  MUX_4X1_8BITS mux_4x1_8bits_2 (
    .A0(A4), .A1(A5), .A2(A6), .A3(A7), .Select(Seletor[1:0]), .Saida(mux_4x1_8bits_2_saida), .Load(Load));
  MUX_2X1_8BITS mux_2x1_8bits_1 (
    .in_1(mux_4x1_8bits_1_saida), .in_2(mux_4x1_8bits_2_saida), .Select(Seletor[2]), .out_5(Saida),
    .Load(Load));
endmodule
