// Logisim project Somador_8Bits.circ as structural Verilog
module main (
  input  [7:0] A,
  input  [7:0] B,
  output [7:0] S,
  output overflow
);

  wire full_adder_1_carry_out, full_adder_2_carry_out, full_adder_3_carry_out, full_adder_4_carry_out,
       full_adder_5_carry_out, full_adder_6_carry_out, full_adder_7_carry_out;

  full_adder full_adder_1 (.Carry_Out(full_adder_1_carry_out), .S(S[0]), .A(A[0]), .B(B[0]), .Carry_In(1'b0));
  full_adder full_adder_2 (
    .Carry_Out(full_adder_2_carry_out), .S(S[1]), .A(A[1]), .B(B[1]), .Carry_In(full_adder_1_carry_out));
  full_adder full_adder_3 (
    .Carry_Out(full_adder_3_carry_out), .S(S[2]), .A(A[2]), .B(B[2]), .Carry_In(full_adder_2_carry_out));
  full_adder full_adder_4 (
    .Carry_Out(full_adder_4_carry_out), .S(S[3]), .A(A[3]), .B(B[3]), .Carry_In(full_adder_3_carry_out));
  full_adder full_adder_5 (
    .Carry_Out(full_adder_5_carry_out), .S(S[4]), .A(A[4]), .B(B[4]), .Carry_In(full_adder_4_carry_out));
  full_adder full_adder_6 (
    .Carry_Out(full_adder_6_carry_out), .S(S[5]), .A(A[5]), .B(B[5]), .Carry_In(full_adder_5_carry_out));
  full_adder full_adder_7 (
    .Carry_Out(full_adder_7_carry_out), .S(S[6]), .A(A[6]), .B(B[6]), .Carry_In(full_adder_6_carry_out));
  full_adder full_adder_8 (.Carry_Out(overflow), .S(S[7]), .A(A[7]), .B(B[7]), .Carry_In(full_adder_7_carry_out));
endmodule
