// Logisim project full_adder.circ as structural Verilog: 2 circuits, main circuit main
module main (
  input  Carry_In,
  input  B,
  input  A,
  output S,
  output Carry_Out
);

  full_adder full_adder_1 (.Carry_Out(Carry_Out), .S(S), .A(A), .B(B), .Carry_In(Carry_In));
endmodule

module full_adder (
  input  A,
  input  B,
  input  Carry_In,
  output S,
  output Carry_Out
);

  wire and_1_out, and_2_out, xor_1_out;

  xor xor_1 (xor_1_out, A, B);
  and and_1 (and_1_out, B, A);
  and and_2 (and_2_out, Carry_In, xor_1_out);
  xor xor_2 (S, xor_1_out, Carry_In);
  or or_1 (Carry_Out, and_2_out, and_1_out);
endmodule
