// Logisim project Extensor De Sinal.circ as structural Verilog: 2 circuits, main circuit main
module main (
  input  [3:0] entrada,
  output [7:0] \saída 
);


  assign \saída  = {{5{entrada[3]}}, entrada[2:0]};
endmodule

module extensor_sinal (
  input  [3:0] entrada,
  output [7:0] \saída 
);


  assign \saída  = {{5{entrada[3]}}, entrada[2:0]};
endmodule
