// Logisim project Maquina De Estados.circ as structural Verilog
module main (
  input  CLOCK,
  input  ENTRADA,
  output \SAÍDA 
);

  wire and_1_out, and_2_out, or_1_out;

  and and_1 (and_1_out, ~\SAÍDA , ENTRADA);  // AND_Gate
  and and_2 (and_2_out, \SAÍDA , ~ENTRADA);  // AND_Gate
  or or_1 (or_1_out, and_1_out, and_2_out);
  D_Flip_Flop ESTADO_ATUAL (.clk(CLOCK), .D(or_1_out), .Q(\SAÍDA ));  // open: Qn, preset, en, reset
endmodule
