// Logisim project Detector Primo.circ as structural Verilog: 1 circuit, main circuit Detector de Número Primo
module \Detector_de_Número_Primo  (
  input  [3:0] _3_2_1_0,
  output S
);

  wire A_B_C_out, A_CD_out, B_CD_out, BC_D_out;

  and A_B_C (A_B_C_out, ~_3_2_1_0[3], ~_3_2_1_0[2], _3_2_1_0[1]);  // AND_Gate
  and A_CD (A_CD_out, ~_3_2_1_0[3], _3_2_1_0[1], _3_2_1_0[0]);  // AND_Gate
  and BC_D (BC_D_out, _3_2_1_0[2], ~_3_2_1_0[1], _3_2_1_0[0]);  // AND_Gate
  and B_CD (B_CD_out, ~_3_2_1_0[2], _3_2_1_0[1], _3_2_1_0[0]);  // AND_Gate
  or or_1 (S, A_B_C_out, A_CD_out, BC_D_out, B_CD_out);

  // Notes on the sheet:
  //   A B C D
  //   Saída =1 é primo
  //   SIMPLIFICADO = A/B/C + A/CD + BC/D + B/CD
  //   NÃO SIMPLIFICADO  = A/B/CD/ + A/B/CD + A/BC/D + A/BCD + AB/CD + ABC/D
endmodule
